# Fritzing sketch esquematico (saved by Fritzing 0.9.3b)

parts:
  Componente2 = Arduino Uno (Rev3)
  Componente3 = Bluetooth HC-05 Macho

nets:
  N1: Componente2.D0/RX, Componente3.TXD
  3V3: Componente2.3V3, Componente3.VCC
  GND: Componente2.GND, Componente3.GND
