# Fritzing sketch esquematico (saved by Fritzing 0.9.3b)
breadboards: 1

parts:
  Componente1 = Arduino Uno (Rev3)
  M2 = DC Motor
  L298N1 = L298N DC motor driver
  M3 = DC Motor  # not connected
  VCC1 = 4 x AAA Battery Mount
  M6 = DC Motor  # not connected
  M7 = DC Motor  # not connected
  L298N3 = L298N DC motor driver
  VCC2 = Battery block 9V

nets:
  N1: Componente1.D8, L298N1.IN4
  N2: Componente1.D9_PWM, L298N1.IN3
  N3: Componente1.D10_PWM/SS, L298N1.IN2
  N4: Componente1.D11_PWM/MOSI, L298N1.IN1
  N5: Componente1.D2, L298N3.IN4
  N6: Componente1.D3_PWM, L298N3.IN3
  N7: Componente1.D4, L298N3.IN2
  N8: Componente1.D5_PWM, L298N3.IN1
  N9: Componente1.5V, VCC1.+
  N10: Componente1.GND, VCC1.-
  N11: M2.pin_1, L298N1.OUT4
  N12: M2.pin_2, L298N1.OUT3
  12V: L298N1.12V, L298N1.5V, L298N3.12V, L298N3.5V, VCC2.+
  GND: L298N1.GND, L298N3.GND, VCC2.-

notes:
  FRONT OF THE CAR

custom parts:
  L298N DC motor driver: 2x DC motor driver with 78M05 positive voltage regulator (7..35 V) L298N: max 46 V, 2 A Set 5 V Enable jumper to enable 5 V regultor (needed for the L298N) and +5 V output at screw terminal or supply external +5 V at screw terminal Set ENA and/or ENB to +5 V to enable motor permanently or supply ENA and/or ENB with PWM signal IN1 and IN2 set rotation directory for motor A (OUT1/OUT2) IN2 and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
